# Fritzing sketch schema_circuito (saved by Fritzing 0.9.3b)
breadboards: 1

parts:
  Part1 = Arduino Uno (Rev3)
  LED1 = LED - 5mm [color="Red (633nm)" package="5 mm [THT]"]
  LED2 = LED - 5mm [color="Green (555nm)" package="5 mm [THT]"]
  LED3 = LED - 5mm [color="Green (555nm)" package="5 mm [THT]"]
  LED4 = LED - 5mm [color="Green (555nm)" package="5 mm [THT]"]
  LED5 = LED - 5mm [color="White (8000K)" package="5 mm [THT]"]
  R1 = Resistor [tolerance=±5% resistance=220 package="0805 [SMD]"]
  R2 = Resistor [tolerance=±5% resistance=220 package="0805 [SMD]"]
  R3 = Resistor [tolerance=±5% resistance=220 package="0805 [SMD]"]
  R4 = Resistor [tolerance=±5% resistance=220 package="0805 [SMD]"]
  R5 = Resistor [tolerance=±5% resistance=220 package="0805 [SMD]"]
  R6 = Resistor [tolerance=±5% resistance=1k package="0805 [SMD]"]
  R7 = Resistor [tolerance=±5% resistance=1k package="0805 [SMD]"]
  S1 = Pushbutton [package="[THT]"]
  S2 = Pushbutton [package="[THT]"]
  R8 = Rotary Potentiometer (Small) [maximum_resistance=100kΩ package=THT]

nets:
  N1: Part1.A0, R8.wiper
  N2: Part1.D8, LED2.anode
  N3: Part1.D9_PWM, LED4.anode
  N4: Part1.D10_PWM/SS, LED5.anode
  N5: Part1.D11_PWM/MOSI, LED1.anode
  N6: Part1.D2, R7.Pin_1, S1.Pin_3, S1.Pin_4
  N7: Part1.D3_PWM, R6.Pin_1, S2.Pin_3, S2.Pin_4
  N8: Part1.D7, LED3.anode
  N9: Part1.5V, S1.Pin_1, S1.Pin_2, S2.Pin_1, S2.Pin_2, R8.leg2
  N10: Part1.GND, R1.Pin_0, R2.Pin_0, R3.Pin_0, R4.Pin_0, R5.Pin_0, R6.Pin_0, R7.Pin_0, R8.leg1
  N11: LED1.cathode, R5.Pin_1
  N12: LED2.cathode, R2.Pin_1
  N13: LED3.cathode, R1.Pin_1
  N14: LED4.cathode, R3.Pin_1
  N15: LED5.cathode, R4.Pin_1
